// Logisim project tructruc.circ as structural Verilog: 3 circuits, main circuit Demi add
module Demi_add (
  input  A,
  input  B,
  output out_3,
  output out_4
);

  xor xor_1 (out_3, A, B);
  and and_1 (out_4, A, B);
endmodule

module add_complet (
  input  A,
  input  B,
  input  C,
  output out_4,
  output out_5
);

  wire demi_add_1_out_3, demi_add_1_out_4, demi_add_2_out_4;

  Demi_add demi_add_1 (.A(B), .B(C), .out_3(demi_add_1_out_3), .out_4(demi_add_1_out_4));
  Demi_add demi_add_2 (.A(A), .B(demi_add_1_out_3), .out_3(out_4), .out_4(demi_add_2_out_4));
  or or_1 (out_5, demi_add_2_out_4, demi_add_1_out_4);
endmodule

module add_4bits (
  input  A0,
  input  B0,
  input  A1,
  input  B1,
  input  A2,
  input  A2_2,
  input  A3,
  input  B3,
  output S0,
  output S1,
  output S2,
  output S3,
  output Retenue
);

  wire add_complet_2_out_5, demi_add_1_out_4;

  Demi_add demi_add_1 (.A(A0), .B(B0), .out_3(S0), .out_4(demi_add_1_out_4));
  add_complet add_complet_1 (.A(demi_add_1_out_4), .B(A1), .C(B1), .out_4(S1), .out_5(S1));
  add_complet add_complet_2 (.A(S1), .B(A2), .C(A2_2), .out_4(S2), .out_5(add_complet_2_out_5));
  add_complet add_complet_3 (.A(add_complet_2_out_5), .B(A3), .C(B3), .out_4(S3), .out_5(Retenue));
endmodule
